// Logisim project nasma_vlsi_final.circ as structural Verilog: 12 circuits, main circuit main
module main (
  input  ring_reset,
  input  in_2,
  input  debug,
  input  clk,
  input  in_5,
  input  in_6,
  input  in_7,
  input  in_8,
  output [3:0] out_9,
  output [7:0] out_10,
  output [7:0] out_11,
  output [7:0] out_12,
  output [7:0] out_13,
  output [7:0] out_14,
  output [7:0] out_15,
  output [7:0] out_16,
  output [7:0] out_17,
  output [7:0] out_18,
  output [7:0] out_19,
  output [7:0] out_20,
  output [7:0] out_21,
  output [7:0] out_22,
  output [7:0] out_23,
  output [7:0] out_24,
  output [7:0] out_25,
  output [7:0] out_26,
  output [7:0] out_27,
  output [7:0] out_28,
  output [3:0] out_29,
  output [3:0] out_30,
  output [7:0] out_31,
  output [7:0] out_32
);

  wire a_in, a_out, alo_1_a_equal_b, alo_1_a_greater_than_b, alo_1_a_less_than_b, alu_out, alu_sub, b_in,
       b_out, comp_out, hlt, ins_reg_in_en, ins_reg_out_en, mar_in_en, pc_en, pc_out_en, ring_en, sram_read,
       sram_wr;
  wire [7:0] auto_load_1_sram_ad_out, auto_load_1_sram_ad_out_en, debug_data, multiplexer_1_out;

  Multiplexer #(.width(8)) multiplexer_1 (
    .in0(auto_load_1_sram_ad_out), .in1({out_10[7:4], out_9}), .out(multiplexer_1_out), .sel(ring_en));
  count count_1 (.pc_en(pc_en), .pc_clk(clk), .pc_reset(in_2), .pc_out_en(pc_out_en), .pc_out(out_9));
  rampart1 rampart1_1 (
    .sram_rd(sram_read), .sram_wr(sram_wr), .sram_d_in(out_32), .mar_d_in(multiplexer_1_out),
    .mar_in_en(mar_in_en), .sram_clk(clk), .sram_d_out({out_10[7:4], out_9}), .out_8(out_13), .out_9(out_14),
    .out_10(out_15), .out_11(out_16), .out_12(out_17), .out_13(out_18), .out_14(out_19), .out_15(out_20),
    .out_16(out_21), .out_17(out_22), .out_18(out_23), .out_19(out_24), .out_20(out_25), .out_21(out_26),
    .out_22(out_27), .out_23(out_28));
  ROM rom_1 (.addr(auto_load_1_sram_ad_out_en), .data(out_32));
  auto_load auto_load_1 (
    .load_en(debug), .in_2(in_6), .load_clk(clk), .load_reset(in_7), .debug(debug), .in_7(in_8),
    .sram_ad_out(auto_load_1_sram_ad_out), .sram_ad_out_en(auto_load_1_sram_ad_out_en), .cs_in(ring_en),
    .sram_wr(sram_wr));  // open: in_5, pc_value
  assign {out_10[7:4], out_9} = debug ? debug_data : 8'bz;  // Controlled_Buffer controlled_buffer_1
  Hex_Digit_Display hex_digit_display_1 (.value(out_11[7:4]));  // open: dp
  Hex_Digit_Display hex_digit_display_2 (.value(out_11[3:0]));  // open: dp
  regis regis_1 (
    .reg_in({out_10[7:4], out_9}), .reg_in_en(a_in), .reg_clk(clk), .reg_out_en(a_out), .reg_int_out(out_11),
    .reg_out({out_10[7:4], out_9}));
  regis regis_2 (
    .reg_in({out_10[7:4], out_9}), .reg_in_en(b_in), .reg_clk(clk), .reg_out_en(b_out), .reg_int_out(out_12),
    .reg_out({out_10[7:4], out_9}));
  IR ir_1 (
    .ins_reg_in({out_10[7:4], out_9}), .ins_reg_in_en(ins_reg_in_en), .clk(clk),
    .ins_reg_out_en(ins_reg_out_en), .add_outs(out_9), .ins_out(out_30));
  Hex_Digit_Display hex_digit_display_3 (.value(out_12[7:4]));  // open: dp
  alo alo_1 (
    .alu_in_1(out_11), .alu_out_en(alu_out), .alu_sub(alu_sub), .comp_out(comp_out), .alu_in_2(out_12),
    .alu_out({out_10[7:4], out_9}), .A_less_than_B(alo_1_a_less_than_b),
    .A_greater_than_B(alo_1_a_greater_than_b), .A_equal_B(alo_1_a_equal_b));  // open: alu_carry_out
  Hex_Digit_Display hex_digit_display_4 (.value(out_12[3:0]));  // open: dp
  Hex_Digit_Display hex_digit_display_5 (.value(out_10[7:4]));  // open: dp
  Hex_Digit_Display hex_digit_display_6 (.value(out_9));  // open: dp
  LED led_1 (.in(alo_1_a_less_than_b));
  LED led_2 (.in(alo_1_a_equal_b));
  LED led_3 (.in(alo_1_a_greater_than_b));
  control_seq control_seq_1 (
    .ring_en(ring_en), .clk(clk), .ring_reset(ring_reset), .ir_msb(out_30), .mar_in_manual(debug),
    .debug(debug), .in_7(in_5), .pc_out(pc_out_en), .mar_in_en(mar_in_en), .pc_en(pc_en),
    .sram_read(sram_read), .ins_reg_out(ins_reg_out_en), .a_in(a_in), .b_in(b_in), .alu_out(alu_out),
    .comp_out(comp_out), .alu_sub(alu_sub), .hlt(hlt), .ins_reg_en(ins_reg_in_en));

  assign out_10[3:0] = out_9;
  assign out_29 = out_9;
  assign out_31 = {out_10[7:4], out_9};

  // Other names for the same wires on the sheet: load_en = debug; mar_in_manual = debug; pc_reset = in_2;
  //   sram_d_in[7:0] = out_32

  // Notes on the sheet:
  //   contents of rom_1 (hex, n*v repeats v):
  //   18 29 30 d0 f0 0 0 0 5 7
  //   A<B
  //   A=B
  //   A>B
endmodule

module regis (
  input  [7:0] reg_in,
  input  reg_in_en,
  input  reg_clk,
  input  reg_out_en,
  output [7:0] reg_int_out,
  output [7:0] reg_out
);

  wire multiplexer_1_out, multiplexer_2_out, multiplexer_3_out, multiplexer_4_out, multiplexer_5_out,
       multiplexer_6_out, multiplexer_7_out, multiplexer_8_out;

  Multiplexer multiplexer_1 (.in0(reg_int_out[7]), .in1(reg_in[7]), .out(multiplexer_1_out), .sel(reg_in_en));
  D_Flip_Flop d_ff_1 (.D(multiplexer_1_out), .clk(reg_clk), .Q(reg_int_out[7]));  // open: Qn, preset, reset
  Multiplexer multiplexer_2 (.in0(reg_int_out[6]), .in1(reg_in[6]), .out(multiplexer_2_out), .sel(reg_in_en));
  assign reg_out[7] = reg_out_en ? reg_int_out[7] : 1'bz;  // Controlled_Buffer controlled_buffer_1
  D_Flip_Flop d_ff_2 (.D(multiplexer_2_out), .clk(reg_clk), .Q(reg_int_out[6]));  // open: Qn, preset, reset
  Multiplexer multiplexer_3 (.in0(reg_int_out[5]), .in1(reg_in[5]), .out(multiplexer_3_out), .sel(reg_in_en));
  assign reg_out[6] = reg_out_en ? reg_int_out[6] : 1'bz;  // Controlled_Buffer controlled_buffer_2
  D_Flip_Flop d_ff_3 (.D(multiplexer_3_out), .clk(reg_clk), .Q(reg_int_out[5]));  // open: Qn, preset, reset
  Multiplexer multiplexer_4 (.in0(reg_int_out[4]), .in1(reg_in[4]), .out(multiplexer_4_out), .sel(reg_in_en));
  assign reg_out[5] = reg_out_en ? reg_int_out[5] : 1'bz;  // Controlled_Buffer controlled_buffer_3
  D_Flip_Flop d_ff_4 (.D(multiplexer_4_out), .clk(reg_clk), .Q(reg_int_out[4]));  // open: Qn, preset, reset
  Multiplexer multiplexer_5 (.in0(reg_int_out[3]), .in1(reg_in[3]), .out(multiplexer_5_out), .sel(reg_in_en));
  assign reg_out[4] = reg_out_en ? reg_int_out[4] : 1'bz;  // Controlled_Buffer controlled_buffer_4
  D_Flip_Flop d_ff_5 (.D(multiplexer_5_out), .clk(reg_clk), .Q(reg_int_out[3]));  // open: Qn, preset, reset
  Multiplexer multiplexer_6 (.in0(reg_int_out[2]), .in1(reg_in[2]), .out(multiplexer_6_out), .sel(reg_in_en));
  assign reg_out[3] = reg_out_en ? reg_int_out[3] : 1'bz;  // Controlled_Buffer controlled_buffer_5
  D_Flip_Flop d_ff_6 (.D(multiplexer_6_out), .clk(reg_clk), .Q(reg_int_out[2]));  // open: Qn, preset, reset
  Multiplexer multiplexer_7 (.in0(reg_int_out[1]), .in1(reg_in[1]), .out(multiplexer_7_out), .sel(reg_in_en));
  assign reg_out[2] = reg_out_en ? reg_int_out[2] : 1'bz;  // Controlled_Buffer controlled_buffer_6
  D_Flip_Flop d_ff_7 (.D(multiplexer_7_out), .clk(reg_clk), .Q(reg_int_out[1]));  // open: Qn, preset, reset
  assign reg_out[1] = reg_out_en ? reg_int_out[1] : 1'bz;  // Controlled_Buffer controlled_buffer_7
  Multiplexer multiplexer_8 (.in0(reg_int_out[0]), .in1(reg_in[0]), .out(multiplexer_8_out), .sel(reg_in_en));
  D_Flip_Flop d_ff_8 (.D(multiplexer_8_out), .clk(reg_clk), .Q(reg_int_out[0]));  // open: Qn, preset, reset
  assign reg_out[0] = reg_out_en ? reg_int_out[0] : 1'bz;  // Controlled_Buffer controlled_buffer_8
endmodule

module alo (
  input  [7:0] alu_in_1,
  input  alu_out_en,
  input  alu_sub,
  input  comp_out,
  input  [7:0] alu_in_2,
  output [7:0] alu_out,
  output alu_carry_out,
  output A_less_than_B,
  output A_greater_than_B,
  output A_equal_B
);

  wire adder_2_cout, adder_3_cout, adder_4_cout, adder_5_cout, adder_6_cout, adder_7_cout, adder_8_cout,
       and_1_out, comparator_1_eq, not_1_out, not_2_out, xor_1_out, xor_2_out, xor_3_out, xor_4_out,
       xor_5_out, xor_6_out, xor_7_out, xor_8_out;
  wire [7:0] adder_8_out;

  xor xor_1 (xor_1_out, alu_in_2[7], alu_sub);
  Adder #(.width(1)) adder_1 (
    .a(alu_in_1[7]), .b(xor_1_out), .out(adder_8_out[7]), .cin(adder_2_cout), .cout(alu_carry_out));
  xor xor_2 (xor_2_out, alu_in_2[6], alu_sub);
  Adder #(.width(1)) adder_2 (
    .a(alu_in_1[6]), .b(xor_2_out), .out(adder_8_out[6]), .cin(adder_3_cout), .cout(adder_2_cout));
  xor xor_3 (xor_3_out, alu_in_2[5], alu_sub);
  Adder #(.width(1)) adder_3 (
    .a(alu_in_1[5]), .b(xor_3_out), .out(adder_8_out[5]), .cin(adder_4_cout), .cout(adder_3_cout));
  xor xor_4 (xor_4_out, alu_in_2[4], alu_sub);
  Adder #(.width(1)) adder_4 (
    .a(alu_in_1[4]), .b(xor_4_out), .out(adder_8_out[4]), .cin(adder_5_cout), .cout(adder_4_cout));
  xor xor_5 (xor_5_out, alu_in_2[3], alu_sub);
  Adder #(.width(1)) adder_5 (
    .a(alu_in_1[3]), .b(xor_5_out), .out(adder_8_out[3]), .cin(adder_6_cout), .cout(adder_5_cout));
  xor xor_6 (xor_6_out, alu_in_2[2], alu_sub);
  Adder #(.width(1)) adder_6 (
    .a(alu_in_1[2]), .b(xor_6_out), .out(adder_8_out[2]), .cin(adder_7_cout), .cout(adder_6_cout));
  xor xor_7 (xor_7_out, alu_in_2[1], alu_sub);
  Adder #(.width(1)) adder_7 (
    .a(alu_in_1[1]), .b(xor_7_out), .out(adder_8_out[1]), .cin(adder_8_cout), .cout(adder_7_cout));
  xor xor_8 (xor_8_out, alu_in_2[0], alu_sub);
  Adder #(.width(1)) adder_8 (.a(alu_in_1[0]), .b(xor_8_out), .out(adder_8_out[0]), .cin(alu_sub), .cout(adder_8_cout));
  Comparator comparator_1 (.a(alu_in_1), .b(alu_in_2), .eq(comparator_1_eq));  // open: gt, lt
  assign alu_out = alu_out_en ? adder_8_out : 8'bz;  // Controlled_Buffer controlled_buffer_1
  assign A_less_than_B = comp_out ? adder_8_out[7] : 1'bz;  // Controlled_Buffer controlled_buffer_2
  assign A_equal_B = comp_out ? comparator_1_eq : 1'bz;  // Controlled_Buffer controlled_buffer_3
  not not_1 (not_1_out, adder_8_out[7]);
  not not_2 (not_2_out, comparator_1_eq);
  and and_1 (and_1_out, not_1_out, not_2_out);
  assign A_greater_than_B = comp_out ? and_1_out : 1'bz;  // Controlled_Buffer controlled_buffer_4
endmodule

module count (
  input  pc_en,
  input  pc_clk,
  input  pc_reset,
  input  pc_out_en,
  output [3:0] pc_out
);

  wire j_k_ff_2_qn, j_k_ff_3_qn, j_k_ff_4_qn;
  wire [3:0] j_k_ff_4_q;

  J_K_Flip_Flop j_k_ff_1 (
    .J(pc_en), .K(pc_en), .clk(j_k_ff_2_qn), .Q(j_k_ff_4_q[3]), .reset(pc_reset));  // open: Qn, preset
  J_K_Flip_Flop j_k_ff_2 (
    .J(pc_en), .K(pc_en), .clk(j_k_ff_3_qn), .Q(j_k_ff_4_q[2]), .Qn(j_k_ff_2_qn), .reset(pc_reset));  // open: preset
  J_K_Flip_Flop j_k_ff_3 (
    .J(pc_en), .K(pc_en), .clk(j_k_ff_4_qn), .Q(j_k_ff_4_q[1]), .Qn(j_k_ff_3_qn), .reset(pc_reset));  // open: preset
  J_K_Flip_Flop j_k_ff_4 (
    .J(pc_en), .K(pc_en), .clk(pc_clk), .Q(j_k_ff_4_q[0]), .Qn(j_k_ff_4_qn), .reset(pc_reset));  // open: preset
  assign pc_out = pc_out_en ? j_k_ff_4_q : 4'bz;  // Controlled_Buffer controlled_buffer_1
endmodule

module sram (
  input  [7:0] data_in,
  input  wr_en,
  input  clk,
  input  cs,
  input  rd_en,
  output [7:0] memory_content,
  output [7:0] data_out
);

  wire and_1_out, and_2_out;

  and and_1 (and_1_out, wr_en, cs);
  and and_2 (and_2_out, cs, rd_en);
  regis regis_1 (
    .reg_in(data_in), .reg_in_en(and_1_out), .reg_clk(clk), .reg_out_en(and_2_out),
    .reg_int_out(memory_content), .reg_out(data_out));
endmodule

module rampart1 (
  input  sram_rd,
  input  sram_wr,
  input  [7:0] sram_d_in,
  input  [7:0] mar_d_in,
  input  mar_in_en,
  input  sram_clk,
  output [7:0] sram_d_out,
  output [7:0] out_8,
  output [7:0] out_9,
  output [7:0] out_10,
  output [7:0] out_11,
  output [7:0] out_12,
  output [7:0] out_13,
  output [7:0] out_14,
  output [7:0] out_15,
  output [7:0] out_16,
  output [7:0] out_17,
  output [7:0] out_18,
  output [7:0] out_19,
  output [7:0] out_20,
  output [7:0] out_21,
  output [7:0] out_22,
  output [7:0] out_23
);

  wire [7:0] controlled_buffer_1_out, regis_1_reg_int_out;
  wire [15:0] decode_4x16_1_dec_out;

  regis regis_1 (
    .reg_in(mar_d_in), .reg_in_en(mar_in_en), .reg_clk(sram_clk), .reg_int_out(regis_1_reg_int_out));  // open: reg_out_en, reg_out
  decode_4x16 decode_4x16_1 (.dec_sel(regis_1_reg_int_out[3:0]), .dec_out(decode_4x16_1_dec_out));
  assign controlled_buffer_1_out = sram_wr ? sram_d_in : 8'bz;  // Controlled_Buffer controlled_buffer_1
  sram sram_1 (
    .data_in(controlled_buffer_1_out), .wr_en(sram_wr), .clk(sram_clk), .cs(decode_4x16_1_dec_out[0]),
    .rd_en(sram_rd), .memory_content(out_8), .data_out(controlled_buffer_1_out));
  sram sram_2 (
    .data_in(controlled_buffer_1_out), .wr_en(sram_wr), .clk(sram_clk), .cs(decode_4x16_1_dec_out[1]),
    .rd_en(sram_rd), .memory_content(out_9), .data_out(controlled_buffer_1_out));
  sram sram_3 (
    .data_in(controlled_buffer_1_out), .wr_en(sram_wr), .clk(sram_clk), .cs(decode_4x16_1_dec_out[2]),
    .rd_en(sram_rd), .memory_content(out_10), .data_out(controlled_buffer_1_out));
  sram sram_4 (
    .data_in(controlled_buffer_1_out), .wr_en(sram_wr), .clk(sram_clk), .cs(decode_4x16_1_dec_out[3]),
    .rd_en(sram_rd), .memory_content(out_11), .data_out(controlled_buffer_1_out));
  sram sram_5 (
    .data_in(controlled_buffer_1_out), .wr_en(sram_wr), .clk(sram_clk), .cs(decode_4x16_1_dec_out[4]),
    .rd_en(sram_rd), .memory_content(out_12), .data_out(controlled_buffer_1_out));
  sram sram_6 (
    .data_in(controlled_buffer_1_out), .wr_en(sram_wr), .clk(sram_clk), .cs(decode_4x16_1_dec_out[5]),
    .rd_en(sram_rd), .memory_content(out_13), .data_out(controlled_buffer_1_out));
  sram sram_7 (
    .wr_en(sram_wr), .clk(sram_clk), .cs(decode_4x16_1_dec_out[6]), .rd_en(sram_rd), .memory_content(out_14),
    .data_out(controlled_buffer_1_out));  // open: data_in
  sram sram_8 (
    .wr_en(sram_wr), .clk(sram_clk), .cs(decode_4x16_1_dec_out[7]), .rd_en(sram_rd), .memory_content(out_15),
    .data_out(controlled_buffer_1_out));  // open: data_in
  sram sram_9 (
    .data_in(controlled_buffer_1_out), .wr_en(sram_wr), .clk(sram_clk), .cs(decode_4x16_1_dec_out[8]),
    .rd_en(sram_rd), .memory_content(out_16), .data_out(controlled_buffer_1_out));
  sram sram_10 (
    .data_in(controlled_buffer_1_out), .wr_en(sram_wr), .clk(sram_clk), .cs(decode_4x16_1_dec_out[9]),
    .rd_en(sram_rd), .memory_content(out_17), .data_out(controlled_buffer_1_out));
  sram sram_11 (
    .data_in(controlled_buffer_1_out), .wr_en(sram_wr), .clk(sram_clk), .cs(decode_4x16_1_dec_out[10]),
    .rd_en(sram_rd), .memory_content(out_18), .data_out(controlled_buffer_1_out));
  sram sram_12 (
    .data_in(controlled_buffer_1_out), .wr_en(sram_wr), .clk(sram_clk), .cs(decode_4x16_1_dec_out[11]),
    .rd_en(sram_rd), .memory_content(out_19), .data_out(controlled_buffer_1_out));
  sram sram_13 (
    .data_in(controlled_buffer_1_out), .wr_en(sram_wr), .clk(sram_clk), .cs(decode_4x16_1_dec_out[12]),
    .rd_en(sram_rd), .memory_content(out_20), .data_out(controlled_buffer_1_out));
  sram sram_14 (
    .data_in(controlled_buffer_1_out), .wr_en(sram_wr), .clk(sram_clk), .cs(decode_4x16_1_dec_out[13]),
    .rd_en(sram_rd), .memory_content(out_21), .data_out(controlled_buffer_1_out));
  sram sram_15 (
    .data_in(controlled_buffer_1_out), .wr_en(sram_wr), .clk(sram_clk), .cs(decode_4x16_1_dec_out[14]),
    .rd_en(sram_rd), .memory_content(out_22), .data_out(controlled_buffer_1_out));
  sram sram_16 (
    .data_in(controlled_buffer_1_out), .wr_en(sram_wr), .clk(sram_clk), .cs(decode_4x16_1_dec_out[15]),
    .rd_en(sram_rd), .memory_content(out_23), .data_out(controlled_buffer_1_out));
  assign sram_d_out = sram_rd ? controlled_buffer_1_out : 8'bz;  // Controlled_Buffer controlled_buffer_2
endmodule

module decode_4x16 (
  input  [3:0] dec_sel,
  output [15:0] dec_out
);

  wire not_1_out, not_2_out, not_3_out, not_4_out;

  not not_1 (not_1_out, dec_sel[3]);
  not not_2 (not_2_out, dec_sel[2]);
  not not_3 (not_3_out, dec_sel[1]);
  not not_4 (not_4_out, dec_sel[0]);
  and and_1 (dec_out[0], not_4_out, not_3_out, not_2_out, not_1_out);
  and and_2 (dec_out[1], dec_sel[0], not_3_out, not_2_out, not_1_out);
  and and_3 (dec_out[2], not_4_out, dec_sel[1], not_2_out, not_1_out);
  and and_4 (dec_out[3], dec_sel[0], dec_sel[1], not_2_out, not_1_out);
  and and_5 (dec_out[4], not_4_out, not_3_out, dec_sel[2], not_1_out);
  and and_6 (dec_out[5], dec_sel[0], not_3_out, dec_sel[2], not_1_out);
  and and_7 (dec_out[6], not_4_out, dec_sel[0], dec_sel[1], not_1_out);
  and and_8 (dec_out[7], dec_sel[0], dec_sel[1], dec_sel[2], not_1_out);
  and and_9 (dec_out[8], not_4_out, not_3_out, not_2_out, dec_sel[3]);
  and and_10 (dec_out[9], dec_sel[0], not_3_out, not_2_out, dec_sel[3]);
  and and_11 (dec_out[10], not_4_out, dec_sel[1], not_2_out, dec_sel[3]);
  and and_12 (dec_out[11], dec_sel[0], dec_sel[1], not_2_out, dec_sel[3]);
  and and_13 (dec_out[12], not_4_out, not_3_out, dec_sel[2], dec_sel[3]);
  and and_14 (dec_out[13], dec_sel[0], not_3_out, dec_sel[2], dec_sel[3]);
  and and_15 (dec_out[14], not_4_out, dec_sel[1], dec_sel[2], dec_sel[3]);
  and and_16 (dec_out[15], dec_sel[0], dec_sel[1], dec_sel[2], dec_sel[3]);
endmodule

module IR (
  input  [7:0] ins_reg_in,
  input  ins_reg_in_en,
  input  clk,
  input  ins_reg_out_en,
  output [3:0] add_outs,
  output [3:0] ins_out
);

  wire [3:0] regis_1_reg_int_out;

  regis regis_1 (
    .reg_in(ins_reg_in), .reg_in_en(ins_reg_in_en), .reg_clk(clk),
    .reg_int_out({ins_out, regis_1_reg_int_out}));  // open: reg_out_en, reg_out
  assign add_outs = ins_reg_out_en ? regis_1_reg_int_out : 4'bz;  // Controlled_Buffer controlled_buffer_1
endmodule

module ring_co (
  input  ring_en,
  input  clk,
  input  ring_reset,
  output T0,
  output T1,
  output T2,
  output T3
);

  wire controlled_buffer_1_out, not_1_out;
  wire [3:0] count_1_pc_out;
  wire [15:0] decode_4x16_1_dec_out;

  assign controlled_buffer_1_out = ring_reset ? ring_reset : 1'bz;  // Controlled_Buffer controlled_buffer_1
  assign controlled_buffer_1_out = not_1_out ? decode_4x16_1_dec_out[5] : 1'bz;  // Controlled_Buffer controlled_buffer_2
  not not_1 (not_1_out, ring_reset);
  count count_1 (
    .pc_en(ring_en), .pc_clk(clk), .pc_reset(controlled_buffer_1_out), .pc_out_en(ring_en),
    .pc_out(count_1_pc_out));
  decode_4x16 decode_4x16_1 (
    .dec_sel(count_1_pc_out),
    .dec_out({decode_4x16_1_dec_out[15:5], T3, T2, T1, T0, decode_4x16_1_dec_out[0]}));
endmodule

module opcode_decoder (
  input  [3:0] ir_msb,
  output LDA,
  output LDB,
  output ADD,
  output COMPARE,
  output HLT
);

  wire [14:0] decode_4x16_1_dec_out;

  decode_4x16 decode_4x16_1 (
    .dec_sel(ir_msb),
    .dec_out({HLT, decode_4x16_1_dec_out[14], COMPARE, decode_4x16_1_dec_out[12:4], ADD, LDB, LDA, decode_4x16_1_dec_out[0]}));
endmodule

module control_seq (
  input  ring_en,
  input  clk,
  input  ring_reset,
  input  [3:0] ir_msb,
  input  mar_in_manual,
  input  debug,
  input  in_7,
  output pc_out,
  output mar_in_en,
  output pc_en,
  output sram_read,
  output ins_reg_out,
  output a_in,
  output b_in,
  output alu_out,
  output comp_out,
  output alu_sub,
  output hlt,
  output ins_reg_en
);

  wire and_1_out, and_2_out, and_3_out, and_4_out, and_5_out, and_6_out, and_7_out, and_8_out, and_9_out,
       multiplexer_1_out, opcode_decoder_1_add, opcode_decoder_1_compare, opcode_decoder_1_hlt,
       opcode_decoder_1_lda, opcode_decoder_1_ldb, or_1_out, ring_co_1_t2, ring_co_1_t3;

  Multiplexer multiplexer_1 (.in0(ring_en), .in1(in_7), .out(multiplexer_1_out), .sel(hlt));
  ring_co ring_co_1 (
    .ring_en(multiplexer_1_out), .clk(clk), .ring_reset(ring_reset), .T0(pc_out), .T1(ins_reg_en),
    .T2(ring_co_1_t2), .T3(ring_co_1_t3));
  opcode_decoder opcode_decoder_1 (
    .ir_msb(ir_msb), .LDA(opcode_decoder_1_lda), .LDB(opcode_decoder_1_ldb), .ADD(opcode_decoder_1_add),
    .COMPARE(opcode_decoder_1_compare), .HLT(opcode_decoder_1_hlt));
  or or_1 (or_1_out, pc_out, and_1_out, and_2_out);
  Multiplexer multiplexer_2 (.in0(or_1_out), .in1(mar_in_manual), .out(mar_in_en), .sel(debug));
  and and_1 (and_1_out, opcode_decoder_1_lda, ring_co_1_t2);
  and and_2 (and_2_out, opcode_decoder_1_ldb, ring_co_1_t2);
  and and_3 (and_3_out, ring_co_1_t3, opcode_decoder_1_lda);
  or or_2 (sram_read, ins_reg_en, and_3_out, and_4_out);
  and and_4 (and_4_out, opcode_decoder_1_ldb, ring_co_1_t3);
  and and_5 (and_5_out, ring_co_1_t2, opcode_decoder_1_lda);
  and and_6 (and_6_out, opcode_decoder_1_ldb, ring_co_1_t2);
  or or_3 (ins_reg_out, and_5_out, and_6_out, and_7_out);
  and and_7 (and_7_out, opcode_decoder_1_add, ring_co_1_t2);
  and and_8 (and_8_out, ring_co_1_t3, opcode_decoder_1_add);
  or or_4 (a_in, and_8_out, and_9_out);
  and and_9 (and_9_out, opcode_decoder_1_lda, ring_co_1_t3);
  and and_10 (b_in, opcode_decoder_1_ldb, ring_co_1_t3);
  and and_11 (alu_out, ring_co_1_t3, opcode_decoder_1_add);
  and and_12 (comp_out, opcode_decoder_1_compare, ring_co_1_t2);
  and and_13 (alu_sub, opcode_decoder_1_compare, ring_co_1_t2);
  and and_14 (hlt, opcode_decoder_1_hlt, ring_en);

  assign pc_en = ins_reg_en;
endmodule

module auto_load (
  input  load_en,
  input  in_2,
  input  load_clk,
  input  load_reset,
  input  [3:0] in_5,
  input  debug,
  input  in_7,
  output [3:0] pc_value,
  output [7:0] sram_ad_out,
  output [7:0] sram_ad_out_en,
  output cs_in,
  output sram_wr
);

  wire j_k_ff_2_qn, j_k_ff_3_qn, j_k_ff_4_qn, multiplexer_1_out, multiplexer_2_out, not_1_out;

  J_K_Flip_Flop j_k_ff_1 (
    .J(multiplexer_2_out), .K(multiplexer_2_out), .clk(j_k_ff_2_qn), .Q(pc_value[3]), .reset(load_reset));  // open: Qn, preset
  not not_1 (not_1_out, load_clk);
  Multiplexer multiplexer_1 (.in0(debug), .in1(in_7), .out(multiplexer_1_out), .sel(cs_in));
  and and_1 (sram_wr, not_1_out, multiplexer_1_out);
  J_K_Flip_Flop j_k_ff_2 (
    .J(multiplexer_2_out), .K(multiplexer_2_out), .clk(j_k_ff_3_qn), .Q(pc_value[2]), .Qn(j_k_ff_2_qn),
    .reset(load_reset));  // open: preset
  J_K_Flip_Flop j_k_ff_3 (
    .J(multiplexer_2_out), .K(multiplexer_2_out), .clk(j_k_ff_4_qn), .Q(pc_value[1]), .Qn(j_k_ff_3_qn),
    .reset(load_reset));  // open: preset
  J_K_Flip_Flop j_k_ff_4 (
    .J(multiplexer_2_out), .K(multiplexer_2_out), .clk(load_clk), .Q(pc_value[0]), .Qn(j_k_ff_4_qn),
    .reset(load_reset));  // open: preset
  Multiplexer multiplexer_2 (.in0(load_en), .in1(in_2), .out(multiplexer_2_out), .sel(cs_in));
  Register register_1 (.D({in_5, pc_value}), .en(load_clk), .clk(load_clk), .Q(sram_ad_out_en));  // open: clr
  and and_2 (cs_in, pc_value[3], pc_value[2], pc_value[1], pc_value[0]);

  assign sram_ad_out = {in_5, pc_value};

  // Notes on the sheet:
  //   Clock
  //   Count Control
  //   Counter Output
endmodule
